# Fritzing sketch smart_fan (saved by Fritzing 0.9.3b)
breadboards: 1

parts:
  U1 = ESP32S-HiLetgo [part_number=ESP32S-HiLetgo]
  Part2 = Jtron 1 Channel Optoisolated Relay Module [package=relay]
  Part3 = DC-DC Power Module (5v)
  TXS0108E_8-Bit_Bi-directional_Level-Shifting_Voltage_Translator1 = TXS0108 [part_number=TXS0108EPW package=TSSOP]
  S1 = Pushbutton [package="[THT]"]
  S2 = Pushbutton [package="[THT]"]
  S3 = Pushbutton [package="[THT]"]
  S4 = Pushbutton [package="[THT]"]
  R1 = Resistor [tolerance=±5% resistance=440 package=THT]
  R2 = Resistor [tolerance=±5% resistance=440 package=THT]
  R3 = Resistor [tolerance=±5% resistance=440 package=THT]
  R4 = Resistor [tolerance=±5% resistance=440 package=THT]
  Part4 = Jtron 1 Channel Optoisolated Relay Module [package=relay]
  Part5 = Jtron 1 Channel Optoisolated Relay Module [package=relay]

nets:
  N1: U1.GPIO17, S4.Pin_4
  N2: U1.GPIO5, S3.Pin_4
  N3: U1.GPIO18, S2.Pin_4
  N4: U1.GPIO19, S1.Pin_4
  GND: U1.GND, Part2.GND, Part3.GND*, R1.Pin_1, R2.Pin_1, R3.Pin_1, R4.Pin_1, Part4.GND, Part5.GND
  VCC: Part2.VCC, Part3.Vout, TXS0108E_8-Bit_Bi-directional_Level-Shifting_Voltage_Translator1.B1, Part4.VCC, Part5.VCC
  N5: S1.Pin_2, R1.Pin_0
  N6: S2.Pin_2, R2.Pin_0
  N7: S3.Pin_2, R3.Pin_0
  N8: S4.Pin_2, R4.Pin_0

notes:
  3v3
  5v
  // GPIO pins
  APP_BTN0 19 // OFF
  APP_BTN1 18 // 33%
  APP_BTN2 5 // 66%
  APP_BTN3 17 // 100%
  APP_OE 27 // ENABLE
  APP_RELAY1 32
  APP_RELAY2 33
  APP_RELAY3 25
  PWR SRC 5V

custom parts:
  ESP32S-HiLetgo: HiLetgo ESP-WROOM-32 ESP32 ESP-32S Development Board 2.4GHz Dual-Mode WiFi + Bluetooth Dual Cores Microcontroller The ESP32 integrated with Antenna switches, RF Balun, power amplifiers, low-noise amplifiers, filters, and management modules, and the entire solution occupies the least area of PCB. 2.4 GHz Wi-Fi plus Bluetooth dual-mode chip, with TSMC Ultra-low power consumption 40nm technology,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
  DC-DC Power Module (5v): DC-DC Power Module based con AMS1117-5.0 Input: DC 6~12V (input power must higher 1V than output power); Output: 5V (+/-0.05V error), 800mA
  TXS0108: This 8-bit non-inverting translator uses two separate configurable power-supply rails. The A port tracks the VCCA pin supply voltage. The VCCA pin accepts any supply voltage between 1.2 V and 3.6 V. The B port tracks the VCCB pin supply voltage. The VCCB pin accepts any supply voltage between 1.65 V and 5.5 V. Two input supply pins allows for low Voltage bidirectional translation between any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
