# Fritzing sketch relay (saved by Fritzing 0.9.3b)
breadboards: 1

parts:
  U1 = ESP32S-HiLetgo [part_number=ESP32S-HiLetgo]
  Part2 = Jtron 1 Channel Optoisolated Relay Module [package=relay]
  Part3 = Logic Level Converter
  Part4 = DC-DC Power Module (5v)
  PIR1 = PIR sensor

nets:
  N1: U1.3.3, Part3.LV
  N2: U1.GPIO4, Part3.TX_LV
  N3: U1.GPIO5, Part3.TX2_LV
  GND: U1.GND, Part2.GND, Part3.GND, Part4.GND*, PIR1.GND
  VCC: Part2.VCC, Part3.HV, Part4.Vout, PIR1.VDD
  N4: Part2.IN1, Part3.TX_HV
  N5: Part3.TX2_HV, PIR1.SIG

notes:
  5v power module
  5v logic level
  3v3 logic level
  Relay -> GPIO4
  PIR -> GPIO5

custom parts:
  ESP32S-HiLetgo: HiLetgo ESP-WROOM-32 ESP32 ESP-32S Development Board 2.4GHz Dual-Mode WiFi + Bluetooth Dual Cores Microcontroller The ESP32 integrated with Antenna switches, RF Balun, power amplifiers, low-noise amplifiers, filters, and management modules, and the entire solution occupies the least area of PCB. 2.4 GHz Wi-Fi plus Bluetooth dual-mode chip, with TSMC Ultra-low power consumption 40nm technology,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
  DC-DC Power Module (5v): DC-DC Power Module based con AMS1117-5.0 Input: DC 6~12V (input power must higher 1V than output power); Output: 5V (+/-0.05V error), 800mA
