# Fritzing sketch stepper (saved by Fritzing 0.9.3b)
breadboards: 1

parts:
  ENCODER1 = Rotary Encoder with Knob
  MD09B1 = A4988 Stepper Motor Driver Carrier
  M1 = Stepper Motor - Bipolar
  Part1 = DC-DC Power Module (5v)
  U1 = ESP32S-HiLetgo [part_number=ESP32S-HiLetgo]
  R2 = Resistor [tolerance=±5% resistance=4.7k package=THT]

nets:
  N1: ENCODER1.no_name_yet#1, U1.GPIO21
  N2: ENCODER1.no_name_yet#3, U1.GPIO19
  N3: ENCODER1.no_name_yet#4, MD09B1.VDD, U1.3.3, R2.Pin_0
  N4: ENCODER1.no_name_yet#5, MD09B1.GROUND, Part1.GND*, U1.GND
  N5: MD09B1.VMOT, Part1.Vout
  N6: MD09B1.OUT_2B, M1.A
  N7: MD09B1.OUT_2A, M1.C
  N8: MD09B1.OUT_1A, M1.B
  N9: MD09B1.OUT_1B, M1.D

notes:
  STEP -> GPIO23
  DIR -> GPIO22
  Output A -> GPIO19
  Output B -> GPIO21
  12v power source for the motor

custom parts:
  Rotary Encoder with Knob: Rotary Encoder with 1/4" Shaft and Knob
  DC-DC Power Module (5v): DC-DC Power Module based con AMS1117-5.0 Input: DC 6~12V (input power must higher 1V than output power); Output: 5V (+/-0.05V error), 800mA
  ESP32S-HiLetgo: HiLetgo ESP-WROOM-32 ESP32 ESP-32S Development Board 2.4GHz Dual-Mode WiFi + Bluetooth Dual Cores Microcontroller The ESP32 integrated with Antenna switches, RF Balun, power amplifiers, low-noise amplifiers, filters, and management modules, and the entire solution occupies the least area of PCB. 2.4 GHz Wi-Fi plus Bluetooth dual-mode chip, with TSMC Ultra-low power consumption 40nm technology,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
