# Fritzing sketch freertos_queue_ex (saved by Fritzing 0.9.3b)
breadboards: 1

parts:
  U1 = ESP32S-HiLetgo [part_number=ESP32S-HiLetgo]
  Mod1 = KY-018 Photoresistor Module [package="Breakout board"]
  Mod2 = KY-018 Photoresistor Module [package="Breakout board"]
  Mod3 = KY-018 Photoresistor Module [package="Breakout board"]

nets:
  VIN: U1.3.3, Mod1.Vin, Mod2.Vin, Mod3.Vin
  N1: U1.GPIO16, Mod3.S
  N2: U1.GPIO17, Mod2.S
  N3: U1.GPIO5, Mod1.S
  N4: U1.GND, Mod1.-, Mod2.-, Mod3.-

notes:
  TILT -> GPIO16
  SHOCK -> GPIO5
  TAP -> GPIO17

custom parts:
  ESP32S-HiLetgo: HiLetgo ESP-WROOM-32 ESP32 ESP-32S Development Board 2.4GHz Dual-Mode WiFi + Bluetooth Dual Cores Microcontroller The ESP32 integrated with Antenna switches, RF Balun, power amplifiers, low-noise amplifiers, filters, and management modules, and the entire solution occupies the least area of PCB. 2.4 GHz Wi-Fi plus Bluetooth dual-mode chip, with TSMC Ultra-low power consumption 40nm technology,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
  KY-018 Photoresistor Module: KY-018 Photoresistor module, used to measure light intensity. It can determine the presence or absence of light.
