# Fritzing sketch lcd_example (saved by Fritzing 0.9.3b)
breadboards: 1

parts:
  U1 = ESP32S-HiLetgo [part_number=ESP32S-HiLetgo]
  Part1 = Logic Level Converter
  Part2 = DC-DC Power Module (5v)
  LCD1 = LCD screen  # not connected
  U2 = PCF8574 [package="DIP16 [THT]"]
  Mod1 = KY-015 Temperature & Humidity Sensor Module [package="Breakout board"]

nets:
  N1: U1.3.3, Part1.LV, Mod1.Vin
  N2: U1.GPIO17, Mod1.S
  GND: U1.GND, Part1.GND, Part2.GND*, U2.GND, Mod1.-
  N3: U1.GPIO21, Part1.TX_LV
  N4: U1.GPIO22, Part1.TX2_LV
  N5: Part1.TX_HV, U2.SDA
  N6: Part1.HV, Part2.Vout, U2.VCC
  N7: Part1.TX2_HV, U2.P0, U2.SCL

notes:
  LCD SDA -> GPIO21
  LCD SCL -> GPIO22
  DHT11 -> GPIO17
  5V source
  5V
  3V3

custom parts:
  ESP32S-HiLetgo: HiLetgo ESP-WROOM-32 ESP32 ESP-32S Development Board 2.4GHz Dual-Mode WiFi + Bluetooth Dual Cores Microcontroller The ESP32 integrated with Antenna switches, RF Balun, power amplifiers, low-noise amplifiers, filters, and management modules, and the entire solution occupies the least area of PCB. 2.4 GHz Wi-Fi plus Bluetooth dual-mode chip, with TSMC Ultra-low power consumption 40nm technology,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
  DC-DC Power Module (5v): DC-DC Power Module based con AMS1117-5.0 Input: DC 6~12V (input power must higher 1V than output power); Output: 5V (+/-0.05V error), 800mA
  KY-015 Temperature & Humidity Sensor Module: KY-015 temperature and humidity sensor module, provides a low-latency serial interface to measure humidity and temperature.
