# Fritzing sketch tft_example (saved by Fritzing 0.9.3b)
breadboards: 1

parts:
  Part1 = TFT 1.8 inch 160x128 w microSD [part_number=358]
  U1 = ESP32S-HiLetgo [part_number=ESP32S-HiLetgo]
  Mod1 = KY-015 Temperature & Humidity Sensor Module [package="Breakout board"]

nets:
  N1: Part1.SCLK, U1.GPIO18
  N2: Part1.MOSI, U1.GPIO23
  N3: Part1.TFTCS, U1.GPIO5
  N4: Part1.TFTDC, U1.GPIO21
  N5: Part1.RESET, U1.GPIO22
  +5V: Part1.+5V, U1.3.3, Mod1.Vin
  GND: Part1.GND, U1.GND, Mod1.-
  N6: U1.GPIO17, Mod1.S

notes:
  RST -> GPIO22
  DC -> GPIO21
  CS -> GPIO5
  MOSI -> GPIO23
  CLK -> GPIO18
  DHT11 -> GPIO17

custom parts:
  TFT 1.8 inch 160x128 w microSD: This lovely little display breakout is the best way to add a small, colorful and bright display to any project. Since the display uses 4-wire SPI to communicate and has its own pixel-addressable frame buffer, it can be used with every kind of microcontroller. Even a very small one with low memory and few pins available! The 1.8" display has 128x160 color pixels.
  ESP32S-HiLetgo: HiLetgo ESP-WROOM-32 ESP32 ESP-32S Development Board 2.4GHz Dual-Mode WiFi + Bluetooth Dual Cores Microcontroller The ESP32 integrated with Antenna switches, RF Balun, power amplifiers, low-noise amplifiers, filters, and management modules, and the entire solution occupies the least area of PCB. 2.4 GHz Wi-Fi plus Bluetooth dual-mode chip, with TSMC Ultra-low power consumption 40nm technology,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
  KY-015 Temperature & Humidity Sensor Module: KY-015 temperature and humidity sensor module, provides a low-latency serial interface to measure humidity and temperature.
