# Fritzing sketch camera_example (saved by Fritzing 0.9.3b)

parts:
  ESP32_-_Back1 = ESP32 - CAM
  PIR1 = PIR sensor

nets:
  3.3V: ESP32_-_Back1.3.3V, PIR1.VDD
  N1: ESP32_-_Back1.GPIO3_/_RX, PIR1.SIG
  GND: ESP32_-_Back1.GND, PIR1.GND

notes:
  GPIO3 -> PIR data
  3v3 -> PIR power
  GND -> GND

custom parts:
  ESP32 - CAM: The ESP32-CAM has a very competitive small-size camera module that can operate independently as a minimum system with a footprint of only 27*40.5*4.5mm and a deep sleep current of up to 6mA.
