# Fritzing sketch esp32cam_programming (saved by Fritzing 0.9.3b)

parts:
  Part2 = FTDI Basic Programmer
  ESP32_-_Back1 = ESP32 - CAM

nets:
  N1: Part2.RXI, ESP32_-_Back1.GPIO1_/_TX
  N2: Part2.TXO, ESP32_-_Back1.GPIO3_/_RX
  N3: Part2.POWER, ESP32_-_Back1.5V
  N4: Part2.GND, ESP32_-_Back1.GND#16
  N5: ESP32_-_Back1.GPIO0, ESP32_-_Back1.GND#12

notes:
  ESP32-CAM - FTDI
  5V - 5V
  GND - GND
  GPIO1/TX - RX
  GPIO3/RX - TX
  GPIO0 to GND

custom parts:
  ESP32 - CAM: The ESP32-CAM has a very competitive small-size camera module that can operate independently as a minimum system with a footprint of only 27*40.5*4.5mm and a deep sleep current of up to 6mA.
