# Fritzing sketch i2s_example (saved by Fritzing 0.9.3b)
breadboards: 1

parts:
  U1 = ESP32S-HiLetgo [part_number=ESP32S-HiLetgo]
  Part1 = Adafruit MAX98357A I2S 3W Class D Amplifier [part_number="Adafruit #3006"]
  SP1 = SPEAKER [package=pcb_mount_speaker]

nets:
  N1: U1.3.3, Part1.VIN
  N2: U1.GPIO25, Part1.BCLK
  N3: U1.GPIO26, Part1.LRCLK
  N4: U1.GPIO22, Part1.DIN
  GND: U1.GND, Part1.GND
  N5: Part1.VO-, SP1.+
  N6: Part1.VO+, SP1.-

notes:
  LRC -> GPIO26
  BCLK -> GPIO25
  DIN -> GPIO22

custom parts:
  ESP32S-HiLetgo: HiLetgo ESP-WROOM-32 ESP32 ESP-32S Development Board 2.4GHz Dual-Mode WiFi + Bluetooth Dual Cores Microcontroller The ESP32 integrated with Antenna switches, RF Balun, power amplifiers, low-noise amplifiers, filters, and management modules, and the entire solution occupies the least area of PCB. 2.4 GHz Wi-Fi plus Bluetooth dual-mode chip, with TSMC Ultra-low power consumption 40nm technology,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
  Adafruit MAX98357A I2S 3W Class D Amplifier: Listen to this good news - we now have an all in one digital audio amp breakout board that works incredibly well with the Raspberry Pi! If you're looking for an easy and low cost way to get you digital sound files bumpin' then the MAX08357 I2S Amp Breakout is for you. It takes standard I2S digital audio input and, not only decodes it into analog, but also amplifies it directly into a speaker.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
