# Fritzing sketch multisensor (saved by Fritzing 0.9.3b)
breadboards: 1

parts:
  U1 = ESP32S-HiLetgo [part_number=ESP32S-HiLetgo]
  Part2 = BME280 Breakout
  Mod1 = KY-012 Active Buzzer Module [package="Breakout board"]
  ENCODER1 = Rotary Encoder with Knob
  PIR1 = PIR sensor
  Grove2 = Grove OLED 128x96
  Part1 = Adafruit TSL2561 [part_number="Adafruit #439"]

nets:
  3.3V: U1.3.3, Part2.3.3V, Mod1.NC, ENCODER1.no_name_yet#5, PIR1.VDD, Grove2.VCC, Part1.3.3V
  N1: U1.GPIO32, Grove2.SDA
  N2: U1.GPIO33, Grove2.SCL
  GND: U1.GND, Part2.GND, Part2.SDO/ADR, Mod1.-, ENCODER1.no_name_yet#4, PIR1.GND, Grove2.GND, Part1.GND
  N3: U1.GPIO4, PIR1.SIG
  N4: U1.GPIO17, Mod1.S
  N5: U1.GPIO18, ENCODER1.no_name_yet#3
  N6: U1.GPIO19, ENCODER1.no_name_yet#1
  N7: U1.GPIO21, Part2.SDI/SDA, Part1.SDA
  N8: U1.GPIO22, Part2.SCK/SCL, Part1.SCL

notes:
  TSL2561 SCL -> GPIO22
  TSL2561 SDA -> GPIO21
  BME280 SCL -> GPIO22
  BME280 SDA -> GPIO21
  OLED SCL -> GPIO33
  OLED SDA -> GPIO32
  ROTENC OutputA -> GPIO19
  ROTENC OutputB -> GPIO18
  Buzzer -> GPIO17
  PIR -> GPIO4

custom parts:
  ESP32S-HiLetgo: HiLetgo ESP-WROOM-32 ESP32 ESP-32S Development Board 2.4GHz Dual-Mode WiFi + Bluetooth Dual Cores Microcontroller The ESP32 integrated with Antenna switches, RF Balun, power amplifiers, low-noise amplifiers, filters, and management modules, and the entire solution occupies the least area of PCB. 2.4 GHz Wi-Fi plus Bluetooth dual-mode chip, with TSMC Ultra-low power consumption 40nm technology,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
  KY-012 Active Buzzer Module: Active Piezoelectric Buzzer Module KY-012, it produces single-tone sound when signal is high. (Special thanks to vanepp for fixing the PCB holes and other errors)
  Rotary Encoder with Knob: Rotary Encoder with 1/4" Shaft and Knob
  Adafruit TSL2561: The TSL2561 luminosity sensor is an advanced digital light sensor, ideal for use in a wide range of light situations. Compared to low cost CdS cells, this sensor is more precise, allowing for exact lux calculations and can be configured for different gain/timing ranges to detect light ranges from up to 0.1 - 40,000+ Lux on the fly. The best part of this sensor is that it contains both infrared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
