# Fritzing sketch uart_example (saved by Fritzing 0.9.3b)
breadboards: 1

parts:
  U1 = ESP32S-HiLetgo [part_number=ESP32S-HiLetgo]
  U2 = ESP32S-HiLetgo [part_number=ESP32S-HiLetgo]
  Mod1 = KY-015 Temperature & Humidity Sensor Module [package="Breakout board"]

nets:
  N1: U1.3.3, U2.3.3, Mod1.Vin
  N2: U1.GPIO17, U2.GPIO16
  N3: U1.GPIO18, Mod1.S
  GND: U1.GND, U2.GND, Mod1.-

notes:
  ESP32-1 (sender)
  -------
  GPIO18 -> DHT11
  GPIO17 (U2TX) -> ESP32-2/GPIO16 (U2RX)
  ESP32-2 (receiver)
  -------
  GPIO16 (U2RX) -> ESP32-1/GPIO17 (U2TX)

custom parts:
  ESP32S-HiLetgo: HiLetgo ESP-WROOM-32 ESP32 ESP-32S Development Board 2.4GHz Dual-Mode WiFi + Bluetooth Dual Cores Microcontroller The ESP32 integrated with Antenna switches, RF Balun, power amplifiers, low-noise amplifiers, filters, and management modules, and the entire solution occupies the least area of PCB. 2.4 GHz Wi-Fi plus Bluetooth dual-mode chip, with TSMC Ultra-low power consumption 40nm technology,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
  KY-015 Temperature & Humidity Sensor Module: KY-015 temperature and humidity sensor module, provides a low-latency serial interface to measure humidity and temperature.
