# Fritzing sketch switch (saved by Fritzing 0.9.3b)
breadboards: 1

parts:
  U1 = ESP32S-HiLetgo [part_number=ESP32S-HiLetgo]
  Part1 = Jtron 1 Channel Optoisolated Relay Module [package=relay]
  LED1 = LED - 3mm [color="Red (633nm)" package="3 mm [THT]"]
  R1 = Resistor [tolerance=±5% resistance=220 package=THT]

nets:
  N1: U1.3.3, Part1.VCC
  N2: U1.GPIO4, Part1.IN1
  N3: U1.GPIO19, R1.Pin_0
  GND: U1.GND, Part1.GND, LED1.cathode
  N4: LED1.anode, R1.Pin_1

notes:
  LED -> GPIO19
  Relay -> GPIO4

custom parts:
  ESP32S-HiLetgo: HiLetgo ESP-WROOM-32 ESP32 ESP-32S Development Board 2.4GHz Dual-Mode WiFi + Bluetooth Dual Cores Microcontroller The ESP32 integrated with Antenna switches, RF Balun, power amplifiers, low-noise amplifiers, filters, and management modules, and the entire solution occupies the least area of PCB. 2.4 GHz Wi-Fi plus Bluetooth dual-mode chip, with TSMC Ultra-low power consumption 40nm technology,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
